# Fritzing sketch MidiController (saved by Fritzing 0.9.3b)
perfboards: 1

parts:
  Pro_Micro1 = Pro Micro
  S8 = Round Pushbutton
  R1 = Resistor [tolerance=±5% resistance=10k package=THT]
  R2 = Resistor [tolerance=±5% resistance=10k package=THT]
  R3 = Resistor [tolerance=±5% resistance=10k package=THT]
  S1 = Round Pushbutton
  S2 = Round Pushbutton
  S3 = Round Pushbutton
  S4 = Round Pushbutton
  S5 = Round Pushbutton
  S6 = Round Pushbutton
  S7 = Round Pushbutton
  S9 = Round Pushbutton
  S10 = Round Pushbutton
  R4 = Resistor [tolerance=±5% resistance=10k package=THT]
  R5 = Resistor [tolerance=±5% resistance=10k package=THT]
  R6 = Resistor [tolerance=±5% resistance=10k package=THT]
  R7 = Resistor [tolerance=±5% resistance=10k package=THT]
  R8 = Resistor [tolerance=±5% resistance=10k package=THT]
  R9 = Resistor [tolerance=±5% resistance=10k package=THT]
  R10 = Resistor [tolerance=±5% resistance=10k package=THT]
  JP2 = Header 10 [package=1x10-2mm-smd]
  JP3 = Header 10 [package=1x10-2mm-smd]
  JP4 = Header 12 [package=1x12_machine-pin-header_lock.004]
  JP5 = Header 12 [package=1x12_machine-pin-header_lock.004]

nets:
  N1: Pro_Micro1.TX1, JP5.1
  N2: Pro_Micro1.RX0, JP5.2
  N3: Pro_Micro1.GND#3, JP5.3
  GND: Pro_Micro1.GND#4, R1.Pin_1, R2.Pin_1, R3.Pin_1, R4.Pin_1, R5.Pin_1, R6.Pin_1, R7.Pin_1, R8.Pin_1, R9.Pin_1, R10.Pin_1
  N4: Pro_Micro1.D2, S8.leg0, R8.Pin_0, JP2.1
  N5: Pro_Micro1.D3, S7.leg0, R7.Pin_0, JP2.2
  N6: Pro_Micro1.D4, S6.leg0, R6.Pin_0, JP2.3, JP5.7
  N7: Pro_Micro1.D5, S5.leg0, R5.Pin_0, JP2.4
  N8: Pro_Micro1.D6, S4.leg0, R4.Pin_0, JP2.5
  N9: Pro_Micro1.D7, R3.Pin_0, S3.leg0, JP2.6, JP5.10
  N10: Pro_Micro1.D8, R2.Pin_0, S2.leg0, JP2.7, JP5.11
  N11: Pro_Micro1.D9, R1.Pin_0, S1.leg0, JP2.8
  N12: Pro_Micro1.D10, S10.leg0, R10.Pin_0, JP2.10
  N13: Pro_Micro1.D16/MOSI, S9.leg0, R9.Pin_0, JP2.9, JP4.11
  N14: Pro_Micro1.D14/MISO, JP4.10
  N15: Pro_Micro1.D15/SCLK, JP4.9
  N16: Pro_Micro1.D18/A0, JP4.8
  N17: Pro_Micro1.D19/A1, JP4.7
  N18: Pro_Micro1.D20/A2, JP4.6
  N19: Pro_Micro1.D21/A3, JP4.5
  5V: Pro_Micro1.VCC, S8.leg1, S1.leg1, S2.leg1, S3.leg1, S4.leg1, S5.leg1, S6.leg1, S7.leg1, S9.leg1, S10.leg1, JP3.1, JP3.2, JP3.3, JP3.4, JP3.5, JP3.6, JP3.7, JP3.8, JP3.9, JP3.10, JP4.4
  N20: Pro_Micro1.RST, JP4.3
  N21: Pro_Micro1.GND#23, JP4.2
  N22: Pro_Micro1.RAW, JP4.1

custom parts:
  Pro Micro: The SparkFun Pro Micro is a complete USB-based microcontoller development system, in a very small footprint, capable of implementing many types of projects. All programming can be done via the USB port.
